# Fritzing sketch Schematic By ArminRT (saved by Fritzing 1.0.5)
breadboards: 1

parts:
  Part1 = Arduino Uno (Rev3)
  LED1 = LED - 5mm [color="Red (633nm)" current=0.030A package="5 mm [THT]"]
  R1 = Resistor [tolerance=±5% power=0.25W resistance=220 package=THT]
  S1 = Pushbutton [package="[THT]"]

nets:
  N1: Part1.GND, R1.Pin_0, S1.Pin_3, S1.Pin_4
  N2: Part1.D2, LED1.anode
  N3: Part1.D4, S1.Pin_1, S1.Pin_2
  N4: LED1.cathode, R1.Pin_1
